// Logisim project lab1.circ as structural Verilog: 5 circuits, main circuit 一位二进制半加器
module \一位二进制半加器  (
  input  A,
  input  B,
  output \本位和S ,
  output \进位C 
);

  xor xor_1 (\本位和S , A, B);
  and and_1 (\进位C , A, B);
endmodule

module \一位二进制全加器  (
  input  A,
  input  B,
  input  Ci,
  output \本位和S ,
  output Co
);

  wire and_1_out, and_2_out, xor_2_out;

  xor xor_1 (\本位和S , xor_2_out, Ci);
  xor xor_2 (xor_2_out, A, B);
  or or_1 (Co, and_1_out, and_2_out);
  and and_1 (and_1_out, xor_2_out, Ci);
  and and_2 (and_2_out, A, B);
endmodule

module \四位二进制串行加法器  (
  input  A3,
  input  A2,
  input  A1,
  input  A0,
  input  B3,
  input  B2,
  input  B1,
  input  B0,
  input  C0,
  output S3,
  output S2,
  output S1,
  output S0,
  output C4
);

  wire \一位二进制全加器_2_co , \一位二进制全加器_3_co , \一位二进制全加器_4_co ;

  \一位二进制全加器  \u_一位二进制全加器_1  (.\本位和S (S3), .Co(C4), .A(A3), .B(B3), .Ci(\一位二进制全加器_2_co ));
  \一位二进制全加器  \u_一位二进制全加器_2  (.\本位和S (S2), .Co(\一位二进制全加器_2_co ), .A(A2), .B(B2), .Ci(\一位二进制全加器_3_co ));
  \一位二进制全加器  \u_一位二进制全加器_3  (.\本位和S (S1), .Co(\一位二进制全加器_3_co ), .A(A1), .B(B1), .Ci(\一位二进制全加器_4_co ));
  \一位二进制全加器  \u_一位二进制全加器_4  (.\本位和S (S0), .Co(\一位二进制全加器_4_co ), .A(A0), .B(B0), .Ci(C0));
endmodule

module \四位二进制并行加法器  (
  input  A3,
  input  A2,
  input  A1,
  input  A0,
  input  B3,
  input  B2,
  input  B1,
  input  B0,
  input  C0,
  output S3,
  output S2,
  output S1,
  output S0,
  output C4
);

  wire and_1_out, and_2_out, and_3_out, and_4_out, and_5_out, and_6_out, and_7_out, and_8_out, and_9_out,
       and_11_out, C1, C2, C3, G0, G1, G2, G3, P0, P1, P2, P3, xor_2_out, xor_4_out, xor_5_out, xor_8_out;

  and and_1 (and_1_out, P3, G2);
  or or_1 (C4, G3, and_1_out, and_2_out, and_3_out, and_4_out);
  and and_2 (and_2_out, P3, P2, G1);
  and and_3 (and_3_out, P3, P2, P1, G0);
  and u_G3 (G3, A3, B3);
  xor u_P3 (P3, A3, B3);
  and and_4 (and_4_out, P3, P2, P1, P0, C0);
  xor xor_1 (S3, xor_2_out, C3);
  xor xor_2 (xor_2_out, A3, B3);
  and and_5 (and_5_out, P2, G1);
  xor u_P2 (P2, A2, B2);
  and u_G2 (G2, A2, B2);
  or or_2 (C3, G2, and_5_out, and_6_out, and_7_out);
  and and_6 (and_6_out, P2, P1, G0);
  xor xor_3 (S2, xor_4_out, C2);
  xor xor_4 (xor_4_out, A2, B2);
  and u_G1 (G1, A1, B1);
  and and_7 (and_7_out, P2, P1, P0, C0);
  xor xor_5 (xor_5_out, A1, B1);
  xor u_P1 (P1, A1, B1);
  or or_3 (C2, G1, and_9_out, and_8_out);
  and and_8 (and_8_out, P1, P0, C0);
  and and_9 (and_9_out, P1, G0);
  xor xor_6 (S1, xor_5_out, C1);
  and and_10 (G0, A0, B0);
  or or_4 (C1, G0, and_11_out);
  and and_11 (and_11_out, P0, C0);
  xor xor_7 (S0, xor_8_out, C0);
  xor xor_8 (xor_8_out, A0, B0);
  xor xor_9 (P0, A0, B0);
endmodule

module \测试1  (
  input  in_1,
  input  [3:0] A,
  input  [3:0] B,
  output out_4
);

  wire [3:0] \四位二进制并行加法器_1_s0 ;

  \四位二进制并行加法器  \u_四位二进制并行加法器_1  (
    .A3(A[3]), .A2(A[2]), .A1(A[1]), .A0(A[0]), .B3(B[3]), .B2(B[2]), .B1(B[1]), .B0(B[0]),
    .S3(\四位二进制并行加法器_1_s0 [3]), .S2(\四位二进制并行加法器_1_s0 [2]), .S1(\四位二进制并行加法器_1_s0 [1]),
    .S0(\四位二进制并行加法器_1_s0 [0]), .C0(in_1), .C4(out_4));
  // Probe on \四位二进制并行加法器_1_s0 

  // Notes on the sheet:
  //   S
endmodule
